# Fritzing sketch Wind-O-Matic 5000 (saved by Fritzing 0.9.3b)
breadboards: 1

parts:
  Mod1 = Raspberry Pi Pico
  Part1 = Adafruit DRV8833 DC/Stepper Motor Driver [part_number="Adafruit #3297"]
  U1 = BUTTON-CONDUCTIVE [package=button-conductive]
  U2 = Voltage Regulator [package=to220-adj]
  M1 = Stepper Motor - Bipolar

nets:
  N1: Mod1.pin_3, Mod1.pin_8, Mod1.pin_13, Mod1.pin_18, Mod1.pin_23, Mod1.pin_28, Mod1.pin_33, Mod1.pin_38, Mod1.pin_42, Part1.GND, U1.2, U2.IN
  N2: Mod1.pin_14, Part1.AIN2
  N3: Mod1.pin_15, Part1.AIN1
  N4: Mod1.pin_16, Part1.BIN2
  N5: Mod1.pin_17, Part1.BIN1
  N6: Mod1.pin_19, Part1.!SLEEP
  N7: Mod1.pin_20, U1.1
  N8: Mod1.pin_39, U2.OUT
  N9: Part1.PWRIN, U2.ADJ
  N10: Part1.AOUT2, M1.B
  N11: Part1.AOUT1, M1.D
  N12: Part1.BOUT1, M1.A
  N13: Part1.BOUT2, M1.C

notes:
  Activate Button
  12V Rail
  5V Regulator

custom parts:
  Raspberry Pi Pico: Raspberry Pi Pico. Based around the RP2040 microcontroller the Pico is a low cost microcontroller device bringing Raspberry Pi quality, cost, and easy of use to the microcontroller space. Jan 2021, Split part in to two versions: tht (this one) and SMD. This one will drill holes for a .1 in header in pcb to allow plugging in the module as well as providing pads to solder the module to the top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
  Adafruit DRV8833 DC/Stepper Motor Driver: Spin two DC motors or step one bi-polar or uni-polar stepper with up to 1.2A per channel using the DRV8833. This motor driver chip is a nice alternative to the TB6612 driver. Like that chip, you get 2 full H-bridges, but this chip is better for low voltage uses (can run from 2.7V up to 10.8V motor power) and has built in current limiting capability. We set it up for 1A current limiting so you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
